// Logisim project Module_design.circ as structural Verilog: 1 circuit, main circuit main
module main (
  input  in_1,
  input  in_2,
  input  in_3,
  input  in_4
);

  wire adder_1_out, adder_2_out, adder_3_out, and_1_out, and_2_out, multiplexer_1_out, multiplexer_2_out,
       multiplexer_3_out, multiplexer_4_out, multiplexer_5_out, multiplexer_6_out, multiplexer_7_out,
       multiplexer_8_out, multiplexer_9_out, multiplexer_10_out, not_1_out, not_2_out, undriven_2,
       undriven_3, undriven_4, undriven_5, undriven_6, undriven_7, undriven_8, undriven_9, undriven_10,
       undriven_11, undriven_12, undriven_13, undriven_14, undriven_15, undriven_16, undriven_17,
       undriven_18, undriven_19, undriven_20, undriven_21, undriven_22, undriven_23, undriven_24,
       undriven_25, undriven_26, undriven_27, undriven_28, undriven_29, undriven_30, undriven_31,
       undriven_32, undriven_33, undriven_34, undriven_35, undriven_36, undriven_37, undriven_38,
       undriven_39, undriven_40, undriven_41, undriven_42, undriven_43, undriven_44, undriven_45;
  wire [3:0] priority_encoder_1_out;
  wire [11:0] undriven;

  not not_1 (not_1_out, in_1);
  Priority_Encoder #(.select(4)) priority_encoder_1 (
    .in0(1'b1), .in1(1'b1), .in2(1'b1), .in3(1'b1), .in4(undriven[0]), .in5(undriven[1]), .in6(undriven[2]),
    .in7(undriven[3]), .in8(undriven[4]), .in9(undriven[5]), .in10(undriven[6]), .in11(undriven[7]),
    .in12(undriven[8]), .in13(undriven[9]), .in14(undriven[10]), .in15(undriven[11]),
    .out(priority_encoder_1_out));  // open: gs, en_out, en_in
  Adder #(.width(1)) adder_1 (.a(not_1_out), .b(1'b1), .out(adder_1_out));  // open: cin, cout
  Multiplexer #(.enable("false")) multiplexer_1 (.in0(in_1), .in1(adder_1_out), .out(multiplexer_1_out), .sel(in_1));
  Multiplexer #(.select(4), .enable("false")) multiplexer_2 (
    .in0(undriven_2), .in1(undriven_2), .in2(undriven_2), .in3(undriven_2), .in4(undriven_2),
    .in5(undriven_2), .in6(undriven_2), .in7(undriven_2), .in8(undriven_23), .in9(undriven_3),
    .in10(undriven_24), .in11(undriven_4), .in12(undriven_25), .in13(undriven_5), .in14(undriven_26),
    .in15(undriven_6), .out(multiplexer_2_out), .sel(priority_encoder_1_out));
  Multiplexer #(.select(4), .enable("false")) multiplexer_3 (
    .in0(undriven_27), .in1(undriven_7), .in2(undriven_28), .in3(undriven_8), .in4(undriven_29),
    .in5(undriven_9), .in6(undriven_30), .in7(undriven_10), .in8(undriven_31), .in9(undriven_11),
    .in10(undriven_32), .in11(undriven_12), .in12(undriven_33), .in13(undriven_13), .in14(undriven_34),
    .in15(undriven_14), .out(multiplexer_3_out), .sel(priority_encoder_1_out));
  Multiplexer #(.select(4), .enable("false")) multiplexer_4 (
    .in0(undriven_35), .in1(undriven_15), .in2(undriven_36), .in3(undriven_16), .in4(undriven_37),
    .in5(undriven_17), .in6(undriven_38), .in7(undriven_18), .in8(undriven_39), .in9(undriven_19),
    .in10(undriven_40), .in11(undriven_20), .in12(undriven_41), .in13(undriven_21), .in14(undriven_42),
    .in15(undriven_22), .out(multiplexer_4_out), .sel(priority_encoder_1_out));
  and and_1 (and_1_out, in_3, undriven_43);
  and and_2 (and_2_out, in_4, undriven_44);
  not not_2 (not_2_out, in_2);
  Adder #(.width(1)) adder_2 (.a(in_3), .b(1'b1), .out(adder_2_out));  // open: cin, cout
  Adder #(.width(1)) adder_3 (.a(in_4), .b(1'b1), .out(adder_3_out));  // open: cin, cout
  Multiplexer #(.enable("false")) multiplexer_5 (
    .in0(undriven_45), .in1(in_3), .out(multiplexer_5_out), .sel(and_2_out));
  Multiplexer #(.enable("false")) multiplexer_6 (
    .in0(adder_3_out), .in1(in_4), .out(multiplexer_6_out), .sel(and_2_out));
  Multiplexer #(.enable("false")) multiplexer_7 (
    .in0(adder_2_out), .in1(multiplexer_5_out), .out(multiplexer_7_out), .sel(and_1_out));
  Multiplexer #(.enable("false")) multiplexer_8 (
    .in0(in_4), .in1(multiplexer_6_out), .out(multiplexer_8_out), .sel(and_1_out));
  Multiplexer #(.enable("false")) multiplexer_9 (
    .in0(multiplexer_8_out), .in1(in_4), .out(multiplexer_9_out), .sel(not_2_out));
  Multiplexer #(.enable("false")) multiplexer_10 (
    .in0(multiplexer_7_out), .in1(in_3), .out(multiplexer_10_out), .sel(not_2_out));

  // Notes on the sheet:
  //   In [11:0]
  //   a [11:0] (input)
  //   twos_to_sign_mag Module Schematic
  //   In [11]
  //   In[11]
  //   count_and_extract Schematic
  //   000
  //   000
  //   000
  //   000
  //   000
  //   000
  //   000
  //   000
  //   001
  //   010
  //   011
  //   100
  //   101
  //   110
  //   111
  //   111
  //   a [3:0]
  //   a [3:0]
  //   a [3:0]
  //   a [3:0]
  //   a [3:0]
  //   a [3:0]
  //   a [3:0]
  //   a [3:0]
  //   a [4:1]
  //   a [5:2]
  //   a [6:3]
  //   a [7:4]
  //   a [8:5]
  //   a [9:6]
  //   a [10:7]
  //   111
  //   000
  //   000
  //   000
  //   000
  //   000
  //   000
  //   000
  //   000
  //   a [0]
  //   a [1]
  //   a [2]
  //   a [3]
  //   a [4]
  //   a [5]
  //   a [6]
  //   1
  //   S
  //   Out [11:0]
  //   b [2:0] (exponent)
  //   significand [3:0]
  //   fifth_bit
  //   fif_bit
  //   sig [3:0]
  //   1111
  //   exp [2:0]
  //   111
  //   rounding Schematic
  //   sig [3:0]
  //   exp + 1
  //   sig + 1
  //   1000
  //   sig [3:0]
  //   out_sig [3:0]
  //   out_exp [2:0]
endmodule
