// Logisim project lab3_schematics.circ as structural Verilog: 1 circuit, main circuit main
module main (
  input  rst,
  input  in_2,
  input  in_3,
  input  in_4
);

  wire adder_1_out, and_1_out, and_2_out, and_3_out, and_4_out, clock_1_out, clock_2_out, clock_3_out,
       d_ff_1_q, d_ff_2_q, d_ff_3_q, demultiplexer_1_out0, demultiplexer_1_out1, demultiplexer_1_out2,
       demultiplexer_1_out3, demultiplexer_2_out0, demultiplexer_2_out1, demultiplexer_2_out2,
       demultiplexer_2_out3, multiplexer_1_out, multiplexer_2_out, not_1_out, not_2_out, register_1_q,
       register_2_q, register_3_q, register_4_q, shift_register_1_out, undriven, undriven_2, undriven_3,
       undriven_4, undriven_5, undriven_6, undriven_7, undriven_8;

  Adder #(.width(1)) adder_1 (.a(d_ff_1_q), .b(1'b1), .out(adder_1_out));  // open: cin, cout
  Clock clock_1 (.out(clock_1_out));
  and and_1 (and_1_out, in_3, 1'b1);
  Clock clock_2 (.out(clock_2_out));
  and and_2 (and_2_out, in_2, and_1_out);
  D_Flip_Flop d_ff_1 (.clk(clock_1_out), .D(adder_1_out), .Q(d_ff_1_q), .preset(rst));  // open: Qn, en, reset
  Shift_Register #(.length(1), .parallel("false")) shift_register_1 (
    .shift(and_2_out), .clk(clock_2_out), .out(shift_register_1_out), .clr(in_4));  // open: in, load, d0, q0
  D_Flip_Flop d_ff_2 (.clk(clock_1_out), .D(adder_1_out), .Q(d_ff_2_q), .preset(rst));  // open: Qn, en, reset
  not not_1 (not_1_out, shift_register_1_out);
  and and_3 (and_3_out, undriven_2, undriven, not_1_out);
  D_Flip_Flop d_ff_3 (.clk(clock_2_out), .D(and_3_out), .Q(d_ff_3_q), .preset(in_4));  // open: Qn, en, reset
  and and_4 (and_4_out, undriven_3, not_2_out);
  Demultiplexer #(.select(2)) demultiplexer_1 (
    .out0(demultiplexer_1_out0), .out1(demultiplexer_1_out1), .out2(demultiplexer_1_out2),
    .out3(demultiplexer_1_out3), .in(undriven_5), .en(undriven_4));  // open: sel
  Demultiplexer #(.select(2)) demultiplexer_2 (
    .out0(demultiplexer_2_out0), .out1(demultiplexer_2_out1), .out2(demultiplexer_2_out2),
    .out3(demultiplexer_2_out3), .in(and_4_out), .en(undriven_4));  // open: sel
  Clock clock_3 (.out(clock_3_out));
  not not_2 (not_2_out, undriven_6);
  Register #(.width(1)) register_1 (
    .D(demultiplexer_1_out0), .en(demultiplexer_2_out0), .Q(register_1_q), .clk(clock_3_out), .clr(undriven_6));
  Register #(.width(1)) register_2 (
    .D(demultiplexer_1_out1), .en(demultiplexer_2_out1), .Q(register_2_q), .clk(clock_3_out), .clr(undriven_6));
  Register #(.width(1)) register_3 (
    .D(demultiplexer_1_out2), .en(demultiplexer_2_out2), .Q(register_3_q), .clk(clock_3_out), .clr(undriven_6));
  Register #(.width(1)) register_4 (
    .D(demultiplexer_1_out3), .en(demultiplexer_2_out3), .Q(register_4_q), .clk(clock_3_out), .clr(undriven_6));
  Multiplexer #(.select(2)) multiplexer_1 (
    .in0(register_1_q), .in1(register_2_q), .in2(register_3_q), .in3(register_4_q), .out(multiplexer_1_out),
    .en(undriven_7));  // open: sel
  Multiplexer #(.select(2)) multiplexer_2 (
    .in0(register_1_q), .in1(register_2_q), .in2(register_3_q), .in3(register_4_q), .out(multiplexer_2_out),
    .en(undriven_8));  // open: sel

  // Notes on the sheet:
  //   clk
  //   clk_en
  //   clk_dv_inc[17:0]
  //   clk_en Schematic
  //   clk_dv[16:0]
  //   clk
  //   btnS
  //   rst
  //   clk_dv_inc[17]
  //   inst_vld Schematic
  //   step_d[1]
  //   step_d[0]
  //   clk_en_d
  //   clk_en
  //   clk_en_d
  //   inst_vld
  //   i_wdata
  //   i_wsel
  //   i_wstb
  //   clk
  //   Register Block Schematic
  //   Four Registers
  //   rst
  //   i_sel_a
  //   i_sel_b
  //   o_data_a
  //   o_data_b
endmodule
